// Logisim project mips-like.circ as structural Verilog: 6 circuits, main circuit PROCESSADOR
module PROCESSADOR (
  input  select_address,
  input  in_2,
  output [31:0] \INSTRUÇÃO ,
  output [1:0] out_4,
  output [5:0] address,
  output [31:0] leitura
);

  wire and_1_out, button_2_out, button_3_out, clock_1_out, comparator_1_eq, comparator_1_gt, \input ,
       input_r, jump0, jump1, load, or_1_out, or_3_out, reset, save, tunnel, UC_mult, UC_ula_op, UC_write_reg;
  wire [3:0] REG_0;
  wire [5:0] counter_1_q;
  wire [7:0] PC_q_2;
  wire [31:0] adder_1_out, bit_extender_1_out, bit_extender_2_out, bit_extender_3_out, bit_extender_4_out,
       multiplexer_2_out, multiplexer_3_out, multiplexer_4_out, PC_q, REG0_D, REG1_D, ula_1_ula_out;

  or or_1 (or_1_out, jump1, save);
  Adder #(.width(32)) adder_1 (.a({PC_q[31:10], PC_q_2, PC_q[1:0]}), .b(32'h4), .out(adder_1_out));  // open: cin, cout
  assign bit_extender_1_out = {{4{1'b0}}, \INSTRUÇÃO [27:0]};  // Bit_Extender bit_extender_1
  assign bit_extender_2_out = {{12{1'b0}}, \INSTRUÇÃO [19:0]};  // Bit_Extender bit_extender_2
  assign bit_extender_3_out = {{28{1'b0}}, \INSTRUÇÃO [23:20]};  // Bit_Extender bit_extender_3
  Multiplexer #(.width(4), .enable("false")) multiplexer_1 (
    .in0(\INSTRUÇÃO [19:16]), .in1(\INSTRUÇÃO [27:24]), .out(REG_0), .sel(or_1_out));
  jump jump_1 (.jump0(jump0), .jump1(jump1), .r(tunnel), .j0_d(out_4[0]), .j1_d(out_4[1]));
  Multiplexer #(.select(2), .width(32), .disabled(0), .enable("false")) multiplexer_2 (
    .in0(adder_1_out), .in1(bit_extender_1_out), .in3(bit_extender_2_out), .out(multiplexer_2_out),
    .sel(out_4));  // open: in2
  or or_2 (tunnel, comparator_1_gt, comparator_1_eq);
  Comparator #(.width(32), .mode("unsigned")) comparator_1 (
    .a(REG0_D), .b(bit_extender_3_out), .gt(comparator_1_gt), .eq(comparator_1_eq));  // open: lt
  Register #(.width(32)) PC (
    .D(multiplexer_2_out), .Q({PC_q[31:10], PC_q_2, PC_q[1:0]}), .clk(and_1_out), .clr(reset));  // open: en
  Button button_1 (.out(reset));
  and and_1 (and_1_out, or_3_out, clock_1_out);
  Clock clock_1 (.out(clock_1_out));
  or or_3 (or_3_out, \INSTRUÇÃO [16], \INSTRUÇÃO [31], \INSTRUÇÃO [30], \INSTRUÇÃO [29], \INSTRUÇÃO [28], \INSTRUÇÃO [27], \INSTRUÇÃO [26], \INSTRUÇÃO [25], \INSTRUÇÃO [24], \INSTRUÇÃO [23], \INSTRUÇÃO [22], \INSTRUÇÃO [21], \INSTRUÇÃO [20], \INSTRUÇÃO [19], \INSTRUÇÃO [18], \INSTRUÇÃO [17], \INSTRUÇÃO [15], \INSTRUÇÃO [14], \INSTRUÇÃO [13], \INSTRUÇÃO [12], \INSTRUÇÃO [11], \INSTRUÇÃO [10], \INSTRUÇÃO [9], \INSTRUÇÃO [8], \INSTRUÇÃO [7], \INSTRUÇÃO [6], \INSTRUÇÃO [5], \INSTRUÇÃO [4], \INSTRUÇÃO [3], \INSTRUÇÃO [2], \INSTRUÇÃO [1], \INSTRUÇÃO [0]);
  assign bit_extender_4_out = {{8{1'b0}}, \INSTRUÇÃO [23:0]};  // Bit_Extender bit_extender_4
  ROM #(.dataWidth(32)) rom_1 (.addr(PC_q_2), .data(\INSTRUÇÃO ));  // open: sel
  Multiplexer #(.width(32), .enable("false")) multiplexer_3 (
    .in0(bit_extender_4_out), .in1(REG1_D), .out(multiplexer_3_out), .sel(input_r));
  UC UC (
    .E3(\INSTRUÇÃO [31]), .E2(\INSTRUÇÃO [30]), .ula_op(UC_ula_op), .E1(\INSTRUÇÃO [29]),
    .E0(\INSTRUÇÃO [28]), .write_reg(UC_write_reg), .\input (\input ), .save(save), .jump0(jump0),
    .jump1(jump1), .mult(UC_mult), .load(load), .input_r(input_r));
  Multiplexer #(.select(2), .width(32), .enable("false")) multiplexer_4 (
    .in0(ula_1_ula_out), .in1(multiplexer_3_out), .in2(leitura), .out(multiplexer_4_out),
    .sel({load, \input }));  // open: in3
  Button button_2 (.out(button_2_out));
  BANCO_DE_REGISTRADORES banco_de_registradores_1 (
    .DATA_WRITE(multiplexer_4_out), .R0_D(REG0_D), .R1_D(REG1_D), .RESET(reset), .RW_2(\INSTRUÇÃO [27:24]),
    .RW(UC_write_reg), .CLK(and_1_out), .R0(REG_0), .R1(\INSTRUÇÃO [23:20]));
  Counter #(.width(6), .max('h3f)) counter_1 (
    .count(in_2), .Q(counter_1_q), .clk(button_2_out), .clr(button_3_out));  // open: load, D, carry
  Button button_3 (.out(button_3_out));
  Multiplexer #(.width(6), .enable("false")) multiplexer_5 (
    .in0(REG1_D[5:0]), .in1(counter_1_q), .out(address), .sel(select_address));
  memoria memoria_1 (.in_1(address), .in_2(REG0_D), .in_3(save), .in_4(and_1_out), .in_5(reset), .out_6(leitura));
  ULA ula_1 (.DATA_0(REG0_D), .DATA_1(REG1_D), .ULA_OUT(ula_1_ula_out), .ULA_OP(UC_ula_op), .mult(UC_mult));

  // Other names for the same wires on the sheet: data[31:0] = \INSTRUÇÃO ; jump[1:0] = out_4;
  //   load_data[31:0] = leitura

  // Notes on the sheet:
  //   REG_0
  //   REG_1
  //   REG_W
  //   contents of rom_1 (hex, n*v repeats v):
  //   22000001 23000004 24000000 25000010 26000020 20000000 50400048 21000000 51400040 8100000 69030000
  //   9910000 9940000 38900000 1120000 40000020 20000 40000018 20000000 5040007c 21000000 51400074 8100000
  //   69030000 9910000 9950000 38900000 1120000 40000054 20000 4000004c 20000000 504000e8 21000000
  //   514000e0 69030000 9910000 9960000 34900000 27000000 574000d8 6a030000 aa70000 7aa00000 6b730000
  //   bb10000 bb50000 7bb00000 7c900000 6aab0000 cca0000 3c900000 7720000 400000a0 1120000 40000088 20000
  //   40000080
  //   DATA_W
  //   BANCO DE REGISTRADORES
  //   REG0_D
  //   REG1_D
  //   ULA
endmodule

module ULA (
  input  [31:0] DATA_0,
  input  ULA_OP,
  input  [31:0] DATA_1,
  input  mult,
  output [31:0] ULA_OUT
);

  wire [31:0] adder_1_out, multiplier_1_out, subtractor_1_out;

  Adder #(.width(32)) adder_1 (.a(DATA_0), .b(DATA_1), .out(adder_1_out));  // open: cin, cout
  Subtractor #(.width(32)) subtractor_1 (.a(DATA_0), .b(DATA_1), .out(subtractor_1_out));  // open: bin, bout
  Multiplier #(.width(32)) multiplier_1 (.a(DATA_0), .b(DATA_1), .out(multiplier_1_out));  // open: cin, cout
  Multiplexer #(.select(2), .width(32), .enable("false")) multiplexer_1 (
    .in0(adder_1_out), .in1(subtractor_1_out), .in3(multiplier_1_out), .out(ULA_OUT), .sel({mult, ULA_OP}));  // open: in2
endmodule

module UC (
  input  E3,
  input  E2,
  input  E1,
  input  E0,
  output ula_op,
  output write_reg,
  output \input ,
  output save,
  output jump0,
  output jump1,
  output mult,
  output load,
  output input_r
);

  wire and_1_out, and_2_out, and_3_out, and_4_out, and_5_out, and_6_out, and_7_out, and_8_out, and_9_out,
       and_10_out, and_11_out, and_12_out, and_13_out, and_14_out, and_15_out, and_17_out, and_18_out,
       and_19_out, not_1_out, not_2_out, not_3_out, not_4_out, not_5_out, not_6_out, not_7_out, not_8_out,
       not_9_out, not_10_out, not_11_out, not_12_out, not_13_out, not_14_out, not_15_out, not_16_out,
       not_17_out, not_18_out, not_19_out, not_20_out, not_21_out, not_22_out;

  not not_1 (not_1_out, E2);
  not not_2 (not_2_out, E1);
  not not_3 (not_3_out, E3);
  not not_4 (not_4_out, E0);
  not not_5 (not_5_out, E3);
  not not_6 (not_6_out, E2);
  and and_1 (and_1_out, not_5_out, not_6_out, not_7_out);
  not not_7 (not_7_out, E1);
  not not_8 (not_8_out, E3);
  not not_9 (not_9_out, E2);
  and and_2 (and_2_out, not_8_out, not_9_out, not_10_out);
  not not_10 (not_10_out, E0);
  not not_11 (not_11_out, E2);
  and and_3 (and_3_out, not_11_out, not_12_out, not_13_out);
  not not_12 (not_12_out, E1);
  not not_13 (not_13_out, E0);
  not not_14 (not_14_out, E3);
  and and_4 (and_4_out, not_14_out, E2, E1);
  not not_15 (not_15_out, E2);
  and and_5 (and_5_out, not_15_out, E1, not_16_out);
  not not_16 (not_16_out, E0);
  not not_17 (not_17_out, E2);
  and and_6 (and_6_out, E3, not_17_out, not_18_out);
  not not_18 (not_18_out, E0);
  and and_7 (and_7_out, E3, E1);
  not not_19 (not_19_out, E2);
  and and_8 (and_8_out, not_19_out, E1, E0);
  and and_9 (and_9_out, E3, E1, E0);
  and and_10 (and_10_out, E2, not_20_out);
  not not_20 (not_20_out, E1);
  and and_11 (and_11_out, E3, E2);
  not not_21 (not_21_out, E1);
  and and_12 (and_12_out, E2, not_21_out, E0);
  and and_13 (and_13_out, E3, E2, E0);
  and and_14 (and_14_out, E2, E1, not_22_out);
  not not_22 (not_22_out, E0);
  and and_15 (and_15_out, E3, E2, E1);
  and and_16 (load, E2, E1, E0);
  and and_17 (and_17_out, not_1_out, not_2_out, E0);
  or or_1 (ula_op, and_17_out, and_18_out, and_19_out);
  and and_18 (and_18_out, not_3_out, E2, E1, not_4_out);
  and and_19 (and_19_out, E3, E0);
  or or_2 (write_reg, and_1_out, and_2_out, and_3_out, and_4_out);
  or or_3 (\input , and_5_out, and_6_out, and_7_out);
  or or_4 (save, and_8_out, and_9_out);
  or or_5 (jump0, and_10_out, and_11_out);
  or or_6 (jump1, and_12_out, and_13_out);
  or or_7 (mult, and_14_out, and_15_out);

  assign input_r = E3;
endmodule

module BANCO_DE_REGISTRADORES (
  input  [31:0] DATA_WRITE,
  input  RW,
  input  [3:0] R0,
  input  [3:0] RW_2,
  input  [3:0] R1,
  input  CLK,
  input  RESET,
  output [31:0] R0_D,
  output [31:0] R1_D
);

  wire demultiplexer_1_out0, demultiplexer_1_out1, demultiplexer_1_out2, demultiplexer_1_out3,
       demultiplexer_1_out4, demultiplexer_1_out5, demultiplexer_1_out6, demultiplexer_1_out7,
       demultiplexer_1_out8, demultiplexer_1_out9, demultiplexer_1_out10, demultiplexer_1_out11,
       demultiplexer_1_out12, demultiplexer_1_out13, demultiplexer_1_out14, demultiplexer_1_out15;
  wire [31:0] register_1_q, register_2_q, register_3_q, register_4_q, register_5_q, register_6_q,
       register_7_q, register_8_q, register_9_q, register_10_q, register_11_q, register_12_q, register_13_q,
       register_14_q, register_15_q, register_16_q;

  Register #(.width(32)) register_1 (
    .D(DATA_WRITE), .en(demultiplexer_1_out0), .Q(register_1_q), .clk(CLK), .clr(RESET));
  Register #(.width(32)) register_2 (
    .D(DATA_WRITE), .en(demultiplexer_1_out1), .Q(register_2_q), .clk(CLK), .clr(RESET));
  Register #(.width(32)) register_3 (
    .D(DATA_WRITE), .en(demultiplexer_1_out2), .Q(register_3_q), .clk(CLK), .clr(RESET));
  Register #(.width(32)) register_4 (
    .D(DATA_WRITE), .en(demultiplexer_1_out3), .Q(register_4_q), .clk(CLK), .clr(RESET));
  Register #(.width(32)) register_5 (
    .D(DATA_WRITE), .en(demultiplexer_1_out4), .Q(register_5_q), .clk(CLK), .clr(RESET));
  Register #(.width(32)) register_6 (
    .D(DATA_WRITE), .en(demultiplexer_1_out5), .Q(register_6_q), .clk(CLK), .clr(RESET));
  Register #(.width(32)) register_7 (
    .D(DATA_WRITE), .en(demultiplexer_1_out6), .Q(register_7_q), .clk(CLK), .clr(RESET));
  Register #(.width(32)) register_8 (
    .D(DATA_WRITE), .en(demultiplexer_1_out7), .Q(register_8_q), .clk(CLK), .clr(RESET));
  Register #(.width(32)) register_9 (
    .D(DATA_WRITE), .en(demultiplexer_1_out8), .Q(register_9_q), .clk(CLK), .clr(RESET));
  Register #(.width(32)) register_10 (
    .D(DATA_WRITE), .en(demultiplexer_1_out9), .Q(register_10_q), .clk(CLK), .clr(RESET));
  Register #(.width(32)) register_11 (
    .D(DATA_WRITE), .en(demultiplexer_1_out10), .Q(register_11_q), .clk(CLK), .clr(RESET));
  Register #(.width(32)) register_12 (
    .D(DATA_WRITE), .en(demultiplexer_1_out11), .Q(register_12_q), .clk(CLK), .clr(RESET));
  Register #(.width(32)) register_13 (
    .D(DATA_WRITE), .en(demultiplexer_1_out12), .Q(register_13_q), .clk(CLK), .clr(RESET));
  Register #(.width(32)) register_14 (
    .D(DATA_WRITE), .en(demultiplexer_1_out13), .Q(register_14_q), .clk(CLK), .clr(RESET));
  Register #(.width(32)) register_15 (
    .D(DATA_WRITE), .en(demultiplexer_1_out14), .Q(register_15_q), .clk(CLK), .clr(RESET));
  Register #(.width(32)) register_16 (
    .D(DATA_WRITE), .en(demultiplexer_1_out15), .Q(register_16_q), .clk(CLK), .clr(RESET));
  Demultiplexer #(.select(4), .enable("false")) demultiplexer_1 (
    .out0(demultiplexer_1_out0), .out1(demultiplexer_1_out1), .out2(demultiplexer_1_out2),
    .out3(demultiplexer_1_out3), .out4(demultiplexer_1_out4), .out5(demultiplexer_1_out5),
    .out6(demultiplexer_1_out6), .out7(demultiplexer_1_out7), .out8(demultiplexer_1_out8),
    .out9(demultiplexer_1_out9), .out10(demultiplexer_1_out10), .out11(demultiplexer_1_out11),
    .out12(demultiplexer_1_out12), .out13(demultiplexer_1_out13), .out14(demultiplexer_1_out14),
    .out15(demultiplexer_1_out15), .in(RW), .sel(RW_2));
  Multiplexer #(.select(4), .width(32), .disabled(0), .enable("false")) multiplexer_1 (
    .in0(register_1_q), .in1(register_2_q), .in2(register_3_q), .in3(register_4_q), .in4(register_5_q),
    .in5(register_6_q), .in6(register_7_q), .in7(register_8_q), .in8(register_9_q), .in9(register_10_q),
    .in10(register_11_q), .in11(register_12_q), .in12(register_13_q), .in13(register_14_q),
    .in14(register_15_q), .in15(register_16_q), .out(R0_D), .sel(R0));
  Multiplexer #(.select(4), .width(32), .disabled(0), .enable("false")) multiplexer_2 (
    .in0(register_1_q), .in1(register_2_q), .in2(register_3_q), .in3(register_4_q), .in4(register_5_q),
    .in5(register_6_q), .in6(register_7_q), .in7(register_8_q), .in8(register_9_q), .in9(register_10_q),
    .in10(register_11_q), .in11(register_12_q), .in12(register_13_q), .in13(register_14_q),
    .in14(register_15_q), .in15(register_16_q), .out(R1_D), .sel(R1));

  // Notes on the sheet:
  //   r0
  //   r1
  //   r2
  //   r3
  //   r4
  //   r5
  //   r6
  //   r7
  //   r8
  //   r9
endmodule

module memoria (
  input  [5:0] in_1,
  input  [31:0] in_2,
  input  in_3,
  input  in_4,
  input  in_5,
  output [31:0] out_6
);

  RAM #(.addrWidth(6), .dataWidth(32), .bus("separate")) ram_1 (
    .addr(in_1), .din(in_2), .data(out_6), .str(in_3), .clk(in_4), .clr(in_5));  // open: sel, ld
endmodule

module jump (
  input  jump0,
  input  jump1,
  input  r,
  output j0_d,
  output j1_d
);

  wire and_2_out, and_3_out, not_1_out;

  not not_1 (not_1_out, jump1);
  and and_1 (j1_d, jump0, jump1, r);
  and and_2 (and_2_out, jump0, not_1_out);
  and and_3 (and_3_out, jump0, r);
  or or_1 (j0_d, and_2_out, and_3_out);
endmodule
